# Fritzing sketch buildbrick (saved by Fritzing 0.9.3b)
breadboards: 1

parts:
  Part2 = Arduino Mega 2560 (Rev3)
  S1 = Pushbutton [package="[SMD]"]
  S2 = Pushbutton [package="[SMD]"]
  R1 = Rotary Potentiometer (Small) [maximum_resistance=100kΩ package=THT]
  R2 = Rotary Potentiometer (Small) [maximum_resistance=100kΩ package=THT]
  J1 = Piezo Speaker
  R3 = Resistor [tolerance=±5% resistance=10k package="0805 [SMD]"]
  R4 = Resistor [tolerance=±5% resistance=10k package="0805 [SMD]"]

nets:
  N1: Part2.A0, R1.wiper
  N2: Part2.A1, R2.wiper
  N3: Part2.D13_PWM, J1.pin2
  N4: Part2.5V, Part2.D2_PWM, Part2.D3_PWM, S1.Pin_3, S1.Pin_4, S2.Pin_3, S2.Pin_4, R1.leg2, R2.leg2
  N5: Part2.GND, R1.leg1, R2.leg1, J1.pin1, R3.Pin_0, R4.Pin_0
  N6: S1.Pin_1, S1.Pin_2, R4.Pin_1
  N7: S2.Pin_1, S2.Pin_2, R3.Pin_1
